// Logisim project s-mips.circ as structural Verilog: 17 circuits, main circuit S-MIPS Board
module S_MIPS_Board (
  input  DESHABILITAR_DISPATCHER,
  output halt,
  output [31:0] MemAddress,
  output [31:0] WriteData_to_Mem
);

  wire Asrc, button_1_out, CLK, CS, d_ff_1_qn, d_ff_3_p1, Halt_t, IorD, LCLR, LoadRAM, LoadRAMOn, LW, MW,
       not_2_out, R_R_W, R_W, ram_dispatcher_1_finished, RCS, RDest, Reset_out, RST, Rw, SF, TTY_EN,
       undriven, undriven_2, undriven_4, ZF;
  wire [1:0] Bank, WSlct;
  wire [2:0] JSlct, KDB;
  wire [3:0] AControl, LMask, Mask, ram_1_read_time, ram_1_write_time, RMask, s_mips_1_mask;
  wire [4:0] Inst_RD, Inst_RS, Inst_RT, Write_Reg;
  wire [6:0] KDB_DATA, TTY_DATA;
  wire [15:0] Addr, LAddr, RAddr, undriven_3;
  wire [31:0] B, Hi_Data, I0, I1, I2, I3, Ime, InstFromMem, LData, Lo_Data, multiplexer_13_out, offset,
       PC_Out, PC_prime, RAM00, RAM01, RAM02, RAM03, ram_1_data_out_0, ram_1_data_out_1, ram_1_data_out_3,
       ram_1_reset_2, RD1, RI0, RI1, RI2, RI3, WD;

  TTY #(.rows(25), .cols(80)) tty_1 (.data(TTY_DATA), .clk(CLK), .we(TTY_EN), .clr(RST));
  Register #(.width(32)) Register_Lo ();  // open: D, en, Q, clk, clr
  Register #(.width(32)) Register_Hi ();  // open: D, en, Q, clk, clr
  not not_1 (LoadRAMOn, ram_dispatcher_1_finished);
  RAM_Dispatcher ram_dispatcher_1 (
    .WriteTime_2(ram_1_write_time), .Clock_2(CLK), .Data_2(LData), .Address(LAddr), .Mask_2(LMask),
    .Finished(ram_dispatcher_1_finished), .Write(LW), .CLR_2(LCLR));
  Keyboard #(.buflen(64)) keyboard_1 (.clk(CLK), .re(KDB[0]), .avail(KDB[2]), .data(KDB_DATA));  // open: clr
  assign offset = {{16{Inst_RD[4]}}, {Inst_RD, InstFromMem[10:0]}};  // Bit_Extender bit_extender_1
  assign offset = {{16{Inst_RD[4]}}, {Inst_RD, InstFromMem[10:0]}};  // Bit_Extender bit_extender_2
  assign Ime = {{16{1'b0}}, {Inst_RD, InstFromMem[10:0]}};  // Bit_Extender bit_extender_3
  Multiplexer #(.width(32), .enable("false")) multiplexer_1 (.in0(WriteData_to_Mem), .in1(Ime), .out(B), .sel(Asrc));
  RAM ram_1 (
    .Address(RAddr), .Data_Out_0(ram_1_data_out_0), .Data_Out_1(ram_1_data_out_1), .Reset_2(ram_1_reset_2),
    .Data_Out_3(ram_1_data_out_3), .Data_In_0(RI0), .Data_In_1(RI1), .Data_In_2_2(RI2), .Data_In_3(RI3),
    .Mask(RMask), .nRead_Write(R_R_W), .Chip_Select(RCS), .Read_Time(ram_1_read_time), .Reset(button_1_out),
    .Write_Time(ram_1_write_time));
  Program_Counter program_counter_1 (.in_1(PC_prime), .in_2(RST), .in_4(CLK), .Actual_Lo(PC_Out));  // open: in_3
  Button button_1 (.out(button_1_out));
  Button button_2 (.out(button_1_out));
  D_Flip_Flop d_ff_1 (
    .clk(CLK), .D(1'b1), .Q(CLK), .Qn(d_ff_1_qn), .preset(undriven), .en(undriven_2), .reset(Reset_out));
  D_Flip_Flop d_ff_2 (
    .clk(CLK), .D(1'b1), .Q(CLK), .Qn(d_ff_1_qn), .preset(undriven), .en(undriven_2), .reset(Reset_out));
  Button Reset (.out(Reset_out));
  Branch_Control branch_control_1 (
    .in_1(JSlct), .in_2(SF), .in_3(ZF), .in_4(PC_Out), .in_5({Inst_RS, Inst_RT, Inst_RD, InstFromMem[10:0]}),
    .in_6(RD1), .in_7(offset), .PC_prime({InstFromMem[31:26], Inst_RS, Inst_RT, Inst_RD, InstFromMem[10:0]}));
  S_MIPS s_mips_1 (
    .Kbd_Enable(KDB[0]), .Address(Addr), .Kbd_Clear(KDB[1]), .Kbd_Available(KDB[2]), .RAM_In_0(I0),
    .Kbd_ASCII_Data(KDB_DATA), .RAM_In_1(I1), .TTY_Enable(TTY_EN), .RAM_In_2(I2), .RAM_In_3(I3),
    .TTY_ASCII_Data(TTY_DATA), .Reset(RST), .RAM_Out_0(ram_1_data_out_0), .Clock(CLK),
    .RAM_Out_1(ram_1_data_out_1), .Stop(halt), .RAM_Out_2(ram_1_reset_2), .RAM_Out_3(ram_1_data_out_3),
    .Mask(s_mips_1_mask), .Read_Time(ram_1_read_time), .Write_Time(ram_1_write_time), .nRead_Write(R_W),
    .Chip_Select(CS));
  // D_Flip_Flop d_ff_3: pin names not known; wires that end beside it: d_ff_3_p1, d_ff_3_p1, Reset_out, LCLR
  or or_1 (RST, LCLR, LoadRAM);
  Clock clock_1 (.out(CLK));
  Clock clock_2 (.out(CLK));
  RAM_Dispatcher ram_dispatcher_2 ();  // open: WriteTime_2, Clock_2, Data_2, Address, Mask_2, Finished, Write, CLR_2
  RegisterFiles registerfiles_1 (
    .Read_Register_1(Inst_RS), .Read_Register_2(Inst_RT), .Write_Register(Write_Reg), .RegWrite(Rw),
    .Clock(CLK), .Reset(RST), .Write_Data(WD), .Read_Data_1(RD1), .Read_Data_2(WriteData_to_Mem));
  ControlUnit controlunit_1 ();  // open: ALUControl, RegWire, MemRead, MemWrite, ALUSrc, RegDest, WriteSlct, JSelct, IorD, Halt
  Multiplexer #(.width(32), .enable("false")) multiplexer_2 (.in0(I0), .in1(LData), .out(RI0), .sel(LoadRAM));
  Multiplexer #(.width(32), .enable("false")) multiplexer_3 (.in0(I1), .in1(LData), .out(RI1), .sel(LoadRAM));
  Multiplexer #(.width(32), .enable("false")) multiplexer_4 (.in0(I2), .in1(LData), .out(RI2), .sel(LoadRAM));
  Multiplexer #(.width(32), .enable("false")) multiplexer_5 (.in0(I3), .in1(LData), .out(RI3), .sel(LoadRAM));
  and and_1 (LoadRAM, ~DESHABILITAR_DISPATCHER, LoadRAMOn);  // AND_Gate
  Alu alu_1 (
    .A(RD1), .B(B), .ALUControl(AControl), .Output(MemAddress), .ZF_2(ZF), .SF_2(SF));  // open: Hi_Lo_Enable, Actual_Lo_2, Actual_Hi
  Multiplexer #(.width(16), .enable("false")) multiplexer_6 (.in0(Addr), .in1(undriven_3), .out(RAddr), .sel(LoadRAM));
  Multiplexer #(.width(16), .enable("false")) multiplexer_7 (.in0(Addr), .in1(undriven_3), .out(RAddr), .sel(LoadRAM));
  Multiplexer #(.width(4), .enable("false")) multiplexer_8 (.in0(Mask), .in1(LMask), .out(RMask), .sel(undriven_4));
  Multiplexer #(.enable("false")) multiplexer_9 (.in0(CS), .in1(LW), .out(RCS), .sel(LoadRAM));
  Multiplexer #(.enable("false")) multiplexer_10 (.in0(R_W), .in1(LW), .out(R_R_W), .sel(LoadRAM));
  Multiplexer #(.width(5), .enable("false")) multiplexer_11 (
    .in0(Inst_RT), .in1(Inst_RD), .out(Write_Reg), .sel(RDest));
  Multiplexer #(.select(2), .width(32), .enable("false")) multiplexer_12 (
    .in0(MemAddress), .in1({InstFromMem[31:26], Inst_RS, Inst_RT, Inst_RD, InstFromMem[10:0]}),
    .in2(Hi_Data), .in3(Lo_Data), .out(WD), .sel(WSlct));
  Multiplexer #(.width(32), .enable("false")) multiplexer_13 (
    .in0(PC_Out), .in1(MemAddress), .out({multiplexer_13_out[31:4], Bank, multiplexer_13_out[1:0]}),
    .sel(IorD));
  Multiplexer #(.width(4), .enable("false")) multiplexer_14 (.in0(4'b0000), .in1(4'b1111), .out(Mask), .sel(MW));
  RAM ram_2 (
    .Address(multiplexer_13_out[19:4]), .Data_Out_0(RAM00), .Data_Out_1(RAM01), .Reset_2(RAM02),
    .Data_Out_3(RAM03), .Data_In_0(WriteData_to_Mem), .Data_In_1(WriteData_to_Mem),
    .Data_In_2_2(WriteData_to_Mem), .Data_In_3(WriteData_to_Mem), .Mask(Mask), .nRead_Write(MW),
    .Chip_Select(not_2_out), .Reset(RST));  // open: Read_Time, Write_Time
  not not_2 (not_2_out, Halt_t);
  Multiplexer #(.select(2), .width(32), .enable("false")) multiplexer_15 (
    .in0(RAM00), .in1(RAM01), .in2(RAM02), .in3(RAM03),
    .out({InstFromMem[31:26], Inst_RS, Inst_RT, Inst_RD, InstFromMem[10:0]}), .sel(Bank));

  // Other names for the same wires on the sheet: AOut[31:0] = MemAddress;
  //   JSize[25:0] = {Inst_RS, Inst_RT, Inst_RD, InstFromMem[10:0]}; InstFromMem[25:11] = {Inst_RS, Inst_RT, Inst_RD};
  //   RD2[31:0] = WriteData_to_Mem

  // Notes on the sheet:
  //   Keyboard
  //   Output
endmodule

module RAM (
  input  [15:0] Address,
  input  [31:0] Data_In_0,
  input  [31:0] Data_In_1,
  input  [31:0] Data_In_2,
  input  [31:0] Data_In_2_2,
  input  [31:0] Data_In_3,
  input  [3:0] Mask,
  input  nRead_Write,
  input  Chip_Select,
  input  Reset,
  output [31:0] Data_Out_0,
  output [31:0] Data_Out_1,
  output [31:0] Reset_2,
  output [31:0] Data_Out_3,
  output [3:0] Read_Time,
  output [3:0] Write_Time
);

  wire and_2_out, and_3_out, and_4_out, and_5_out, and_6_out, and_7_out, and_8_out, and_9_out, Changed, CLK,
       comparator_2_eq, comparator_3_eq, comparator_4_eq, comparator_5_eq, Count, demultiplexer_3_out0, Idle,
       Idle_q, Load, Load0, Load1, nand_1_out, or_1_out, or_2_out, or_3_out, or_4_out, or_5_out, or_6_out,
       or_8_out, or_9_out, or_10_out, or_11_out, Proc_q, undriven, Update_Mem, Zero_Time;
  wire [3:0] counter_1_q, multiplexer_1_out, subtractor_1_out;
  wire [31:0] register_1_q, register_2_q, register_3_q, register_4_q, register_5_q;

  // Probe on 4'b0011
  // Probe on 4'b0010
  Multiplexer #(.width(4), .enable("false")) multiplexer_1 (
    .in0(4'b0011), .in1(4'b0010), .out(multiplexer_1_out), .sel(nRead_Write));
  or or_1 (or_1_out, Idle, Update_Mem);
  or or_2 (or_2_out, ~Chip_Select, Reset);  // OR_Gate
  Subtractor #(.width(4)) subtractor_1 (.a(multiplexer_1_out), .b(4'b0010), .out(subtractor_1_out));  // open: bin, bout
  D_Flip_Flop u_Idle (.clk(CLK), .D(or_1_out), .Q(Idle_q), .preset(or_2_out));  // open: Qn, en, reset
  Demultiplexer #(.enable("false")) demultiplexer_1 (.out0(Idle), .out1(Load0), .in(Idle_q), .sel(Changed));
  // Probe on counter_1_q
  Counter #(.width(4), .max('hf)) counter_1 (
    .load(Load), .D(subtractor_1_out), .count(Count), .Q(counter_1_q), .clk(CLK), .clr(or_3_out));  // open: carry
  or or_3 (or_3_out, ~Chip_Select, Reset);  // OR_Gate
  Comparator #(.width(4), .mode("unsigned")) comparator_1 (
    .a(4'b0000), .b(counter_1_q), .eq(Zero_Time));  // open: gt, lt
  or or_4 (or_4_out, Count, Load0, Load1);
  Register #(.width(32)) register_1 (.D(Data_In_0), .en(Chip_Select), .Q(register_1_q), .clk(CLK), .clr(or_5_out));
  or or_5 (or_5_out, ~Chip_Select, Reset);  // OR_Gate
  Register #(.width(32)) register_2 (.D(Data_In_1), .en(Chip_Select), .Q(register_2_q), .clk(CLK), .clr(or_6_out));
  or or_6 (or_6_out, ~Chip_Select, Reset);  // OR_Gate
  or or_7 (or_6_out, ~Chip_Select, Reset);  // OR_Gate
  Register #(.width(32)) register_3 (.D(Data_In_2), .en(Chip_Select), .Q(register_3_q), .clk(CLK), .clr(or_8_out));
  or or_8 (or_8_out, ~Chip_Select, Reset);  // OR_Gate
  Register #(.width(32)) register_4 (.D(Data_In_3), .en(Chip_Select), .Q(register_4_q), .clk(CLK), .clr(or_9_out));
  or or_9 (or_9_out, ~Chip_Select, Reset);  // OR_Gate
  Register #(.width(32)) register_5 (
    .D({{11{1'b1}}, nRead_Write, {2{Mask[3]}}, Mask[1:0], Address}), .en(Chip_Select), .Q(register_5_q),
    .clk(CLK), .clr(or_10_out));
  Register #(.width(32)) register_6 (
    .D({{11{1'b1}}, nRead_Write, {2{Mask[3]}}, Mask[1:0], Address}), .en(Chip_Select), .Q(register_5_q),
    .clk(CLK), .clr(or_10_out));
  or or_10 (or_10_out, ~Chip_Select, Reset);  // OR_Gate
  D_Flip_Flop Proc (.clk(CLK), .D(or_4_out), .Q(Proc_q), .reset(or_11_out));  // open: Qn, preset, en
  or or_11 (or_11_out, ~Chip_Select, Reset);  // OR_Gate
  Demultiplexer #(.enable("false")) demultiplexer_2 (
    .out0(Count), .out1(Update_Mem), .in(demultiplexer_3_out0), .sel(Zero_Time));
  Demultiplexer #(.enable("false")) demultiplexer_3 (
    .out0(demultiplexer_3_out0), .out1(Load1), .in(Proc_q), .sel(Changed));
  Clock clock_1 (.out(CLK));
  Comparator #(.width(32)) comparator_2 (.a(register_2_q), .b(Data_In_1), .eq(comparator_2_eq));  // open: gt, lt
  Comparator #(.width(32)) comparator_3 (.a(register_3_q), .b(Data_In_2), .eq(comparator_3_eq));  // open: gt, lt
  Comparator #(.width(32)) comparator_4 (.a(register_4_q), .b(Data_In_3), .eq(comparator_4_eq));  // open: gt, lt
  Comparator #(.width(32)) comparator_5 (
    .a(register_5_q), .b({{11{1'b1}}, nRead_Write, {2{Mask[3]}}, Mask[1:0], Address}), .eq(comparator_5_eq));  // open: gt, lt
  nand nand_1 (nand_1_out, comparator_5_eq, undriven, comparator_2_eq, comparator_3_eq, comparator_4_eq);
  and and_1 (Changed, nand_1_out, Chip_Select);
  or or_12 (Load, Count, Load1, Load0);
  and and_2 (and_2_out, Mask[0], Update_Mem, nRead_Write);
  and and_3 (and_3_out, Mask[1], Update_Mem, nRead_Write);
  and and_4 (and_4_out, Mask[2], Update_Mem, nRead_Write);
  and and_5 (and_5_out, Mask[3], Update_Mem, nRead_Write);
  RAM_part #(.addrWidth(16), .dataWidth(32), .bus("separate")) ram_1 (
    .addr(Address), .din(Data_In_0), .data(Data_Out_0), .str(and_2_out), .sel(Chip_Select), .clk(CLK),
    .ld(and_6_out), .clr(Reset));
  and and_6 (and_6_out, ~nRead_Write, Idle);  // AND_Gate
  RAM_part #(.addrWidth(16), .dataWidth(32), .bus("separate")) ram_2 (
    .addr(Address), .din(Data_In_1), .data(Data_Out_1), .str(and_3_out), .sel(Chip_Select),
    .clk(Chip_Select), .ld(and_7_out), .clr(Reset));
  and and_7 (and_7_out, ~nRead_Write, Idle);  // AND_Gate
  RAM_part #(.addrWidth(16), .dataWidth(32), .bus("separate")) ram_3 (
    .addr(Address), .din(Data_In_2), .data(Reset_2), .str(and_4_out), .sel(Chip_Select), .clk(CLK),
    .ld(and_8_out), .clr(Reset));
  RAM_part #(.addrWidth(16), .dataWidth(32), .bus("separate")) ram_4 (
    .addr(Address), .din(Data_In_2), .data(Reset_2), .str(and_4_out), .sel(Chip_Select), .clk(CLK),
    .ld(and_8_out), .clr(Reset));
  and and_8 (and_8_out, ~nRead_Write, Idle);  // AND_Gate
  RAM_part #(.addrWidth(16), .dataWidth(32), .bus("separate")) ram_5 (
    .addr(Address), .din(Data_In_3), .data(Data_Out_3), .str(and_5_out), .sel(Chip_Select), .clk(CLK),
    .ld(and_9_out), .clr(Reset));
  and and_9 (and_9_out, ~nRead_Write, Idle);  // AND_Gate

  assign Data_In_2_2 = Data_In_2;
  assign Read_Time = 4'b0011;
  assign Write_Time = 4'b0010;

  // Other names for the same wires on the sheet: M0 = Mask[0]; M1 = Mask[1]; M3 = Mask[3]; RW = nRead_Write;
  //   CLR = Reset; CS = Chip_Select; Data_Out_2[31:0] = Reset_2; Load2 = Count; M2 = Mask[2]

  // Notes on the sheet:
  //   NO MODIFICAR
  //   excepto quizás los valores RT y WT
  //   BANK0
  //   BANK1
  //   BANK2
  //   BANK3
endmodule

module S_MIPS (
  input  Kbd_Available,
  input  [6:0] Kbd_ASCII_Data,
  input  [31:0] RAM_Out_0,
  input  [31:0] RAM_Out_1,
  input  Reset,
  input  [31:0] RAM_Out_2,
  input  Clock,
  input  [31:0] RAM_Out_3,
  input  [3:0] Read_Time,
  input  [3:0] Write_Time,
  output Kbd_Enable,
  output [15:0] Address,
  output Kbd_Clear,
  output TTY_Enable,
  output [6:0] TTY_ASCII_Data,
  output Stop,
  output [31:0] RAM_In_0,
  output [31:0] RAM_In_1,
  output [31:0] RAM_In_2,
  output [31:0] RAM_In_3,
  output [3:0] Mask,
  output nRead_Write,
  output Chip_Select
);


  // Other names for the same wires on the sheet: CLK = Clock; CLR = Reset; CS = Chip_Select;
  //   KBD_AVAIL = Kbd_Available; KBD_CLR = Kbd_Clear; KBD_DATA[6:0] = Kbd_ASCII_Data; RAM_A[15:0] = Address;
  //   RAM_INPUT_0[31:0] = RAM_In_0; RAM_INPUT_1[31:0] = RAM_In_1; RAM_INPUT_2[31:0] = RAM_In_2;
  //   RAM_INPUT_3[31:0] = RAM_In_3; RAM_MASK[3:0] = Mask; RAM_OUTPUT_0[31:0] = RAM_Out_0;
  //   RAM_OUTPUT_1[31:0] = RAM_Out_1; RAM_OUTPUT_2[31:0] = RAM_Out_2; RAM_OUTPUT_3[31:0] = RAM_Out_3;
  //   RW = nRead_Write; TTY_DATA[6:0] = TTY_ASCII_Data

  // Notes on the sheet:
  //   RAM ADDRESS
  //   DATA FROM RAM
  //   DATA TO RAM
  //   DATA WRITE MASK
  //   RAM TIMING
  //   RAM CONTROL
  //   KEYBOARD
  //   TTY
  //   SEQUENCING
endmodule

module RAM_Dispatcher (
  input  [3:0] WriteTime,
  input  [3:0] WriteTime_2,
  input  Clock,
  input  Clock_2,
  input  CLR,
  input  CLR_2,
  output [31:0] Data,
  output [31:0] Data_2,
  output [15:0] Address,
  output [3:0] Mask,
  output [3:0] Mask_2,
  output Finished,
  output Write
);

  wire counter_1_carry, CurrentAddress_carry, demultiplexer_2_out1, demultiplexer_4_out1, End, IDLE_q,
       IncAddr, Load, or_1_out, or_3_out, undriven, undriven_3, undriven_4, undriven_5, undriven_6, While_q,
       WriteEnd;
  wire [3:0] counter_1_q;
  wire [31:0] CurrentAddress_q, undriven_2;

  Counter #(.width(32), .max('hffffffff)) CurrentAddress (
    .load(undriven), .D(undriven_2), .count(IncAddr),
    .Q({CurrentAddress_q[31:18], Address, CurrentAddress_q[1:0]}), .carry(CurrentAddress_carry), .clk(Clock),
    .clr(CLR));
  Counter #(.width(32), .max('hffffffff)) CurrentAddress_2 (
    .load(undriven), .D(undriven_2), .count(IncAddr),
    .Q({CurrentAddress_q[31:18], Address, CurrentAddress_q[1:0]}), .carry(CurrentAddress_carry), .clk(Clock),
    .clr(CLR));
  or or_1 (or_1_out, IncAddr, demultiplexer_4_out1, Finished);
  or or_2 (or_1_out, IncAddr, demultiplexer_4_out1, Finished);
  D_Flip_Flop IDLE (.clk(Clock), .D(or_1_out), .Q(IDLE_q), .preset(CLR));  // open: Qn, en, reset
  Demultiplexer #(.enable("false")) demultiplexer_1 (.out0(Load), .out1(Finished), .in(IDLE_q), .sel(End));
  D_Flip_Flop While (.clk(Clock), .D(or_3_out), .Q(While_q), .reset(CLR));  // open: Qn, preset, en
  or or_3 (or_3_out, Write, Load);
  RAM_part #(.addrWidth(18), .dataWidth(32)) ram_1 (
    .addr({Address, CurrentAddress_q[1:0]}), .data(Data), .sel(undriven_3), .clk(Clock), .ld(undriven_4),
    .clr(undriven_5));
  RAM_part #(.addrWidth(18), .dataWidth(32)) ram_2 (
    .addr({Address, CurrentAddress_q[1:0]}), .data(Data), .sel(undriven_3), .clk(Clock), .ld(undriven_4),
    .clr(undriven_5));
  Demultiplexer #(.enable("false")) demultiplexer_2 (
    .out0(Write), .out1(demultiplexer_2_out1), .in(While_q), .sel(WriteEnd));
  Demultiplexer #(.enable("false")) demultiplexer_3 (
    .out0(Write), .out1(demultiplexer_2_out1), .in(While_q), .sel(WriteEnd));
  Decoder #(.select(2)) decoder_1 (
    .out0(Mask[0]), .out1(Mask[1]), .out2(Mask[2]), .out3(Mask[3]), .sel(CurrentAddress_q[1:0]));  // open: en
  Demultiplexer #(.enable("false")) demultiplexer_4 (
    .out0(IncAddr), .out1(demultiplexer_4_out1), .in(demultiplexer_2_out1), .sel(End));
  Demultiplexer #(.enable("false")) demultiplexer_5 (
    .out0(IncAddr), .out1(demultiplexer_4_out1), .in(demultiplexer_2_out1), .sel(End));
  Counter #(.width(4), .max('hf)) counter_1 (
    .load(Load), .D(WriteTime), .count(Write), .Q(counter_1_q), .carry(counter_1_carry), .clk(Clock),
    .clr(undriven_6));
  Counter #(.width(4), .max('hf)) counter_2 (
    .load(Load), .D(WriteTime), .count(Write), .Q(counter_1_q), .carry(counter_1_carry), .clk(Clock),
    .clr(undriven_6));
  Comparator #(.width(32)) comparator_1 (.a(Data), .b({32{1'b1}}), .eq(End));  // open: gt, lt
  Comparator #(.width(4)) comparator_2 (.a(4'b0000), .b(counter_1_q), .eq(WriteEnd));  // open: gt, lt

  assign Clock_2 = Clock;
  assign CLR_2 = CLR;
  assign Data_2 = Data;
  assign Mask_2 = Mask;
  assign WriteTime_2 = WriteTime;

  // Other names for the same wires on the sheet: CLK = Clock; Count = Write; WT[3:0] = WriteTime
endmodule

module Alu (
  input  [31:0] A,
  input  [31:0] B,
  input  [3:0] ALUControl,
  output Hi_Lo_Enable,
  output [31:0] Output,
  output ZF,
  output ZF_2,
  output SF,
  output SF_2,
  output [31:0] Actual_Lo,
  output [31:0] Actual_Lo_2,
  output [31:0] Actual_Hi
);

  wire comparator_1_eq, comparator_2_eq, comparator_3_gt, multiplexer_7_out, SF_div, SF_mult, SF_other,
       subtractor_1_bout, undriven_2, ZF_div_mult, ZF_other;
  wire [31:0] adder_1_out, and_2_out, bit_extender_1_out, bit_extender_2_out, div_Hi, div_Lo, divu_Hi,
       divu_Lo, mul_Hi, mul_Lo, mulu_Hi, mulu_Lo, nor_1_out, or_1_out, or_3_out, OutP1, subtractor_1_out,
       undriven, xor_1_out;

  // Probe on Actual_Hi
  // Probe on Actual_Hi
  // Probe on A
  Multiplexer #(.width(32), .enable("false")) multiplexer_1 (
    .in0(OutP1), .in1(Actual_Lo), .out(Output), .sel(ALUControl[3]));
  and and_1 (Hi_Lo_Enable, ALUControl[2], ALUControl[3]);
  // Probe on Actual_Lo
  // Probe on B
  Adder #(.width(32)) adder_1 (.a(A), .b(B), .out(adder_1_out));  // open: cin, cout
  Subtractor #(.width(32)) subtractor_1 (
    .a(A), .b(B), .out(subtractor_1_out), .bin(undriven_2), .bout(subtractor_1_bout));
  Subtractor #(.width(32)) subtractor_2 (
    .a(A), .b(B), .out(subtractor_1_out), .bin(undriven_2), .bout(subtractor_1_bout));
  assign and_2_out = A & B;  // AND_Gate and_2, 32 bits wide
  assign or_1_out = A | B;  // OR_Gate or_1, 32 bits wide
  assign or_1_out = A | B;  // OR_Gate or_2, 32 bits wide
  assign nor_1_out = ~(A | B);  // NOR_Gate nor_1, 32 bits wide
  assign xor_1_out = A ^ B;  // XOR_Gate xor_1, 32 bits wide
  Comparator #(.width(32)) comparator_1 (.a(A), .b(B), .eq(comparator_1_eq));  // open: gt, lt
  Comparator #(.width(32), .mode("unsigned")) comparator_2 (.a(A), .b(B), .eq(comparator_2_eq));  // open: gt, lt
  Multiplier #(.width(32)) multiplier_1 (.a(A), .b(B), .out(mulu_Lo), .cin(undriven), .cout(mulu_Hi));
  Multiplier #(.width(32)) multiplier_2 (.a(A), .b(B), .out(mulu_Lo), .cin(undriven), .cout(mulu_Hi));
  multiplier_signed multiplier_signed_1 (.A(A), .B(B), .Hi(mul_Hi), .Lo(mul_Lo));
  Divider #(.width(32)) divider_1 (.a(A), .b(B), .out(divu_Lo), .rem(divu_Hi));  // open: upper
  divider_signed divider_signed_1 (.A(A), .B(B), .Hi_2(div_Hi), .Lo(div_Lo));
  assign bit_extender_1_out = {{31{1'b0}}, comparator_1_eq};  // Bit_Extender bit_extender_1
  assign bit_extender_2_out = {{31{1'b0}}, comparator_2_eq};  // Bit_Extender bit_extender_2
  // Probe on OutP1
  Multiplexer #(.select(3), .width(32), .enable("false")) multiplexer_2 (
    .in0(adder_1_out), .in1(subtractor_1_out), .in2(and_2_out), .in3(or_1_out), .in4(nor_1_out),
    .in5(xor_1_out), .in6(bit_extender_1_out), .in7(bit_extender_2_out), .out(OutP1), .sel(ALUControl[2:0]));
  Multiplexer #(.select(3), .width(32), .enable("false")) multiplexer_3 (
    .in0(adder_1_out), .in1(subtractor_1_out), .in2(and_2_out), .in3(or_1_out), .in4(nor_1_out),
    .in5(xor_1_out), .in6(bit_extender_1_out), .in7(bit_extender_2_out), .out(OutP1), .sel(ALUControl[2:0]));
  Multiplexer #(.select(2), .width(32), .enable("false")) multiplexer_4 (
    .in0(mulu_Lo), .in1(mul_Lo), .in2(divu_Lo), .in3(div_Lo), .out(Actual_Lo), .sel(ALUControl[1:0]));
  Comparator #(.width(32)) comparator_3 (.a(OutP1), .b({32{1'b0}}), .gt(comparator_3_gt), .eq(ZF_other), .lt(SF_other));
  Comparator #(.width(32)) comparator_4 (.a(OutP1), .b({32{1'b0}}), .gt(comparator_3_gt), .eq(ZF_other), .lt(SF_other));
  Multiplexer #(.select(2), .width(32), .enable("false")) multiplexer_5 (
    .in0(mulu_Hi), .in1(mul_Hi), .in2(divu_Hi), .in3(div_Hi), .out(Actual_Hi), .sel(ALUControl[1:0]));
  assign or_3_out = Actual_Lo | Actual_Hi;  // OR_Gate or_3, 32 bits wide
  Comparator #(.width(32)) comparator_5 (.a(or_3_out), .b({32{1'b0}}), .eq(ZF_div_mult));  // open: gt, lt
  and and_3 (SF_div, Actual_Lo[31], 1'b1);
  Multiplexer #(.enable("false")) multiplexer_6 (.in0(ZF_other), .in1(ZF_div_mult), .out(ZF), .sel(Hi_Lo_Enable));
  Multiplexer #(.enable("false")) multiplexer_7 (
    .in0(SF_mult), .in1(SF_div), .out(multiplexer_7_out), .sel(ALUControl[1]));
  Multiplexer #(.enable("false")) multiplexer_8 (.in0(SF_other), .in1(multiplexer_7_out), .out(SF), .sel(Hi_Lo_Enable));

  assign Actual_Lo_2 = Actual_Lo;
  assign SF_2 = SF;
  assign ZF_2 = ZF;

  // Other names for the same wires on the sheet: ALU_Decoder[2:0] = ALUControl[2:0];
  //   Hi_Lo_Decoder[1:0] = ALUControl[1:0]; select_SF_mult_div = ALUControl[1]; is_mult_or_div = ALUControl[3];
  //   Hi[31:0] = Actual_Hi; Lo[31:0] = Actual_Lo

  // Notes on the sheet:
  //   Processing Input Info
  //   Input
  //   Output
  //   and
  //   or
  //   or
  //   not
  //   xor
  //   slt
  //   slt
  //   sltu
  //   sltu
  //   Processing Data
  //   Processing Data
  //   Processing Flags
  //   Processing Flags
endmodule

module multiplier_signed (
  input  [31:0] A,
  input  [31:0] B,
  output [31:0] Hi,
  output [31:0] Lo
);

  wire adder_1_cout, is_negative;
  wire [31:0] bit_extender_1_out, Hi_1, Hi_2, Hi_3, Hi_4, Lo_1, Lo_2, Lo_3, Lo_4, Negaitive_Hi, Negaitive_Lo,
       negator_1_out, negator_2_out, negator_3_out, negator_4_out, not_1_out, not_2_out, Positive_Hi,
       Positive_Lo;

  Negator #(.width(32)) negator_1 (.in(B), .out(negator_1_out));
  // Probe on B
  // Probe on B
  Multiplier #(.width(32)) multiplier_1 (.a(A), .b(B), .out(Lo_1), .cout(Hi_1));  // open: cin
  Multiplier #(.width(32)) multiplier_2 (.a(A), .b(negator_1_out), .out(Lo_2), .cout(Hi_2));  // open: cin
  // Probe on A
  Negator #(.width(32)) negator_2 (.in(A), .out(negator_2_out));
  Negator #(.width(32)) negator_3 (.in(A), .out(negator_3_out));
  Negator #(.width(32)) negator_4 (.in(B), .out(negator_4_out));
  xor xor_1 (is_negative, A[31], B[31]);
  xor xor_2 (is_negative, A[31], B[31]);
  Multiplier #(.width(32)) multiplier_3 (.a(negator_2_out), .b(B), .out(Lo_3), .cout(Hi_3));  // open: cin
  Multiplier #(.width(32)) multiplier_4 (.a(negator_3_out), .b(negator_4_out), .out(Lo_4), .cout(Hi_4));  // open: cin
  // Probe on {A[31], B[31]}
  // Probe on Hi
  // Probe on Hi
  Multiplexer #(.select(2), .width(32), .enable("false")) multiplexer_1 (
    .in0(Hi_1), .in1(Hi_2), .in2(Hi_3), .in3(Hi_4), .out(Positive_Hi), .sel({A[31], B[31]}));
  Multiplexer #(.select(2), .width(32), .enable("false")) multiplexer_2 (
    .in0(Lo_1), .in1(Lo_2), .in2(Lo_3), .in3(Lo_4), .out(Positive_Lo), .sel({A[31], B[31]}));
  // Probe on Lo
  // Probe on Lo
  assign bit_extender_1_out = {{31{1'b0}}, adder_1_cout};  // Bit_Extender bit_extender_1
  assign not_1_out = ~Positive_Lo;  // NOT_Gate not_1, 32 bits wide
  assign not_2_out = ~Positive_Hi;  // NOT_Gate not_2, 32 bits wide
  Multiplexer #(.width(32), .enable("false")) multiplexer_3 (
    .in0(Positive_Hi), .in1(Negaitive_Hi), .out(Hi), .sel(is_negative));
  Adder #(.width(32)) adder_1 (.a(not_1_out), .b(32'h1), .out(Negaitive_Lo), .cout(adder_1_cout));  // open: cin
  Adder #(.width(32)) adder_2 (.a(bit_extender_1_out), .b(not_2_out), .out(Negaitive_Hi));  // open: cin, cout
  Multiplexer #(.width(32), .enable("false")) multiplexer_4 (
    .in0(Positive_Lo), .in1(Negaitive_Lo), .out(Lo), .sel(is_negative));

  // Other names for the same wires on the sheet: B_b31 = B[31]; mult_selector[1:0] = {A[31], B[31]}; A_b31 = A[31]

  // Notes on the sheet:
  //   A>0   B>0
  //   A>0   B>0
  //   A>0   B<0
  //   Inputs
  //   Prueba por casos
  //   Prueba por casos
  //   A < 0    B < 0
  //   A < 0    B < 0
  //   A<0   B>0
  //   A<0   B>0
  //   Outputs
  //   Outputs
  //   Procesing Data
  //   Procesing Data
endmodule

module divider_signed (
  input  [31:0] A,
  input  [31:0] B,
  output [31:0] Hi,
  output [31:0] Hi_2,
  output [31:0] Lo
);

  wire B_b31, is_negative, undriven_2;
  wire [31:0] Hi_1, Hi_2_t, Hi_3, Hi_4, Lo_1, Lo_2, Lo_3, Lo_4, Negaitive_Hi, Negaitive_Lo, negator_1_out,
       negator_2_out, negator_3_out, negator_5_out, not_1_out, not_2_out, Positive_Hi, Positive_Lo, undriven;

  Divider #(.width(32)) divider_1 (.a(A), .b(B), .out(Lo_1), .rem(Hi_1));  // open: upper
  // Probe on Hi_1
  Divider #(.width(32)) divider_2 (.a(A), .b(negator_1_out), .out(Lo_2), .rem(Hi_2_t));  // open: upper
  Negator #(.width(32)) negator_1 (.in(B), .out(negator_1_out));
  // Probe on A
  // Probe on B
  // Probe on B
  Negator #(.width(32)) negator_2 (.in(A), .out(negator_2_out));
  Negator #(.width(32)) negator_3 (.in(A), .out(negator_3_out));
  Negator #(.width(32)) negator_4 (.in(A), .out(negator_3_out));
  Negator #(.width(32)) negator_5 (.in(B), .out(negator_5_out));
  Negator #(.width(32)) negator_6 (.in(B), .out(negator_5_out));
  xor xor_1 (is_negative, A[31], B_b31);
  Divider #(.width(32)) divider_3 (.a(negator_2_out), .b(B), .out(Lo_3), .rem(Hi_3));  // open: upper
  Divider #(.width(32)) divider_4 (.a(negator_3_out), .b(negator_5_out), .out(Lo_4), .upper(undriven), .rem(Hi_4));
  Divider #(.width(32)) divider_5 (.a(negator_3_out), .b(negator_5_out), .out(Lo_4), .upper(undriven), .rem(Hi_4));
  // Probe on {A[31], B_b31}
  // Probe on Hi
  Multiplexer #(.select(2), .width(32), .enable("false")) multiplexer_1 (
    .in0(Hi_1), .in1(Hi_2_t), .in2(Hi_3), .in3(Hi_4), .out(Positive_Hi), .sel({A[31], B_b31}));
  Multiplexer #(.select(2), .width(32), .enable("false")) multiplexer_2 (
    .in0(Lo_1), .in1(Lo_2), .in2(Lo_3), .in3(Lo_4), .out(Positive_Lo), .sel({A[31], B_b31}));
  // Probe on Lo
  // Probe on Lo
  assign not_1_out = ~Positive_Lo;  // NOT_Gate not_1, 32 bits wide
  Adder #(.width(32)) adder_1 (.a(not_1_out), .b(32'h1), .out(Negaitive_Lo));  // open: cin, cout
  Multiplexer #(.width(32), .enable("false")) multiplexer_3 (
    .in0(Positive_Lo), .in1(Negaitive_Lo), .out(Lo), .sel(undriven_2));
  assign not_2_out = ~Positive_Hi;  // NOT_Gate not_2, 32 bits wide
  assign not_2_out = ~Positive_Hi;  // NOT_Gate not_3, 32 bits wide
  Adder #(.width(32)) adder_2 (.a(not_2_out), .b(32'h1), .out(Negaitive_Hi));  // open: cin, cout
  Multiplexer #(.width(32), .enable("false")) multiplexer_4 (
    .in0(Positive_Hi), .in1(Negaitive_Hi), .out(Hi), .sel(is_negative));
  Multiplexer #(.width(32), .enable("false")) multiplexer_5 (
    .in0(Positive_Hi), .in1(Negaitive_Hi), .out(Hi), .sel(is_negative));

  assign Hi_2 = Hi;

  // Other names for the same wires on the sheet: div_selector[1:0] = {A[31], B_b31}; A_b31 = A[31]

  // Notes on the sheet:
  //   A>0   B>0
  //   A>0   B>0
  //   A>0   B<0
  //   Inputs
  //   Inputs
  //   Prueba por casos
  //   Prueba por casos
  //   A < 0    B < 0
  //   A<0   B>0
  //   A<0   B>0
  //   Outputs
  //   Procesing Data
endmodule

module RegisterFiles (
  input  [4:0] Read_Register_1,
  input  [4:0] Read_Register_2,
  input  [31:0] Write_Data,
  input  [4:0] Write_Register,
  input  RegWrite,
  input  Clock,
  input  Reset,
  output [31:0] Read_Data_1,
  output [31:0] Read_Data_2
);

  wire and_1_out, and_2_out, and_3_out, and_4_out, and_5_out, and_6_out, and_7_out, and_8_out, and_9_out,
       and_10_out, and_11_out, and_12_out, and_13_out, and_14_out, and_15_out, and_16_out, and_17_out,
       and_18_out, and_19_out, and_20_out, and_21_out, and_22_out, and_23_out, and_24_out, and_25_out,
       and_26_out, and_27_out, and_28_out, and_29_out, and_30_out, and_31_out, and_32_out, D0, D1, D2, D3,
       D4, D5, D6, D7, D8, D9, D10, D11, D12, D13, D14, D15, D16, D17, D18, D19, D20, D21, D22, D23, D24,
       D25, D26, D27, D28, D29, D30, D31;
  wire [31:0] R0, R1, R2, R3, R4, R5, R6, R7, R8, R9, R10, R11, R12, R13, R14, R15, R16, R17, R18, R19, R20,
       R21, R22, R23, R24, R25, R26, R27, R28, R29, R30, R31;

  Decoder #(.select(5), .enable("false")) decoder_1 (
    .out0(D0), .out1(D1), .out2(D2), .out3(D3), .out4(D4), .out5(D5), .out6(D6), .out7(D7), .out8(D8),
    .out9(D9), .out10(D10), .out11(D11), .out12(D12), .out13(D13), .out14(D14), .out15(D15), .out16(D16),
    .out17(D17), .out18(D18), .out19(D19), .out20(D20), .out21(D21), .out22(D22), .out23(D23), .out24(D24),
    .out25(D25), .out26(D26), .out27(D27), .out28(D28), .out29(D29), .out30(D30), .out31(D31),
    .sel(Write_Register));
  Multiplexer #(.select(5), .width(32), .enable("false")) multiplexer_1 (
    .in0(R0), .in1(R1), .in2(R7), .in3(R3), .in4(R4), .in5(R5), .in6(R15), .in7(R7), .in8(R8), .in9(R9),
    .in10(R10), .in11(R11), .in12(R12), .in13(R13), .in14(R14), .in15(R15), .in16(R16), .in17(R17),
    .in18(R18), .in19(R19), .in20(R20), .in21(R21), .in22(R22), .in23(R23), .in24(R24), .in25(R25),
    .in26(R26), .in27(R27), .in28(R28), .in29(R29), .in30(R30), .in31(R31), .out(Read_Data_1),
    .sel(Read_Register_1));
  Multiplexer #(.select(5), .width(32), .enable("false")) multiplexer_2 (
    .in0(R0), .in1(R1), .in2(R2), .in3(R3), .in4(R4), .in5(R5), .in6(R6), .in7(R7), .in8(R8), .in9(R9),
    .in10(R10), .in11(R11), .in12(R12), .in13(R13), .in14(R14), .in15(R15), .in16(R16), .in17(R17),
    .in18(R18), .in19(R19), .in20(R20), .in21(R21), .in22(R22), .in23(R23), .in24(R24), .in25(R25),
    .in26(R26), .in27(R27), .in28(R28), .in29(R29), .in30(R30), .in31(R31), .out(Read_Data_2),
    .sel(Read_Register_2));
  and and_1 (and_1_out, D0, RegWrite);
  and and_2 (and_2_out, D1, RegWrite);
  and and_3 (and_3_out, D2, RegWrite);
  and and_4 (and_4_out, D3, RegWrite);
  and and_5 (and_5_out, D8, RegWrite);
  and and_6 (and_6_out, D9, RegWrite);
  and and_7 (and_7_out, D10, RegWrite);
  and and_8 (and_8_out, D11, RegWrite);
  and and_9 (and_9_out, D16, RegWrite);
  and and_10 (and_10_out, D17, RegWrite);
  and and_11 (and_11_out, D18, RegWrite);
  and and_12 (and_12_out, D19, RegWrite);
  and and_13 (and_13_out, D24, RegWrite);
  and and_14 (and_14_out, D25, RegWrite);
  and and_15 (and_15_out, D26, RegWrite);
  and and_16 (and_16_out, D27, RegWrite);
  Register #(.width(32)) register_1 (.D(Write_Data), .en(and_1_out), .Q(R0), .clk(Clock), .clr(Reset));
  Register #(.width(32)) register_2 (.D(Write_Data), .en(and_2_out), .Q(R1), .clk(Clock), .clr(Reset));
  Register #(.width(32)) register_3 (.D(Write_Data), .en(and_3_out), .Q(R2), .clk(Clock), .clr(Reset));
  Register #(.width(32)) register_4 (.D(Write_Data), .en(and_4_out), .Q(R3), .clk(Clock), .clr(Reset));
  Register #(.width(32)) register_5 (.D(Write_Data), .en(and_5_out), .Q(R8), .clk(Clock), .clr(Reset));
  Register #(.width(32)) register_6 (.D(Write_Data), .en(and_6_out), .Q(R9), .clk(Clock), .clr(Reset));
  Register #(.width(32)) register_7 (.D(Write_Data), .en(and_7_out), .Q(R10), .clk(Clock), .clr(Reset));
  Register #(.width(32)) register_8 (.D(Write_Data), .en(and_8_out), .Q(R11), .clk(Clock), .clr(Reset));
  Register #(.width(32)) register_9 (.D(Write_Data), .en(and_9_out), .Q(R16), .clk(Clock), .clr(Reset));
  Register #(.width(32)) register_10 (.D(Write_Data), .en(and_10_out), .Q(R17), .clk(Clock), .clr(Reset));
  Register #(.width(32)) register_11 (.D(Write_Data), .en(and_11_out), .Q(R18), .clk(Clock), .clr(Reset));
  Register #(.width(32)) register_12 (.D(Write_Data), .en(and_12_out), .Q(R19), .clk(Clock), .clr(Reset));
  Register #(.width(32)) register_13 (.D(Write_Data), .en(and_13_out), .Q(R24), .clk(Clock), .clr(Reset));
  Register #(.width(32)) register_14 (.D(Write_Data), .en(and_14_out), .Q(R25), .clk(Clock), .clr(Reset));
  Register #(.width(32)) register_15 (.D(Write_Data), .en(and_15_out), .Q(R26), .clk(Clock), .clr(Reset));
  Register #(.width(32)) register_16 (.D(Write_Data), .en(and_16_out), .Q(R27), .clk(Clock), .clr(Reset));
  and and_17 (and_17_out, D4, RegWrite);
  and and_18 (and_18_out, D5, RegWrite);
  and and_19 (and_19_out, D6, RegWrite);
  and and_20 (and_20_out, D7, RegWrite);
  and and_21 (and_21_out, D12, RegWrite);
  and and_22 (and_22_out, D13, RegWrite);
  and and_23 (and_23_out, D14, RegWrite);
  and and_24 (and_24_out, D15, RegWrite);
  and and_25 (and_25_out, D20, RegWrite);
  and and_26 (and_26_out, D21, RegWrite);
  and and_27 (and_27_out, D22, RegWrite);
  and and_28 (and_28_out, D23, RegWrite);
  and and_29 (and_29_out, D12, RegWrite);
  and and_30 (and_30_out, D13, RegWrite);
  and and_31 (and_31_out, D14, RegWrite);
  and and_32 (and_32_out, D15, RegWrite);
  Register #(.width(32)) register_17 (.D(Write_Data), .en(and_17_out), .Q(R4), .clk(Clock), .clr(Reset));
  Register #(.width(32)) register_18 (.D(Write_Data), .en(and_18_out), .Q(R5), .clk(Clock), .clr(Reset));
  Register #(.width(32)) register_19 (.D(Write_Data), .en(and_19_out), .Q(R6), .clk(Clock), .clr(Reset));
  Register #(.width(32)) register_20 (.D(Write_Data), .en(and_20_out), .Q(R7), .clk(Clock), .clr(Reset));
  Register #(.width(32)) register_21 (.D(Write_Data), .en(and_21_out), .Q(R12), .clk(Clock), .clr(Reset));
  Register #(.width(32)) register_22 (.D(Write_Data), .en(and_22_out), .Q(R13), .clk(Clock), .clr(Reset));
  Register #(.width(32)) register_23 (.D(Write_Data), .en(and_23_out), .Q(R14), .clk(Clock), .clr(Reset));
  Register #(.width(32)) register_24 (.D(Write_Data), .en(and_24_out), .Q(R15), .clk(Clock), .clr(Reset));
  Register #(.width(32)) register_25 (.D(Write_Data), .en(and_25_out), .Q(R20), .clk(Clock), .clr(Reset));
  Register #(.width(32)) register_26 (.D(Write_Data), .en(and_26_out), .Q(R21), .clk(Clock), .clr(Reset));
  Register #(.width(32)) register_27 (.D(Write_Data), .en(and_27_out), .Q(R22), .clk(Clock), .clr(Reset));
  Register #(.width(32)) register_28 (.D(Write_Data), .en(and_28_out), .Q(R23), .clk(Clock), .clr(Reset));
  Register #(.width(32)) register_29 (.D(Write_Data), .en(and_29_out), .Q(R12), .clk(Clock), .clr(Reset));
  Register #(.width(32)) register_30 (.D(Write_Data), .en(and_30_out), .Q(R13), .clk(Clock), .clr(Reset));
  Register #(.width(32)) register_31 (.D(Write_Data), .en(and_31_out), .Q(R14), .clk(Clock), .clr(Reset));
  Register #(.width(32)) register_32 (.D(Write_Data), .en(and_32_out), .Q(R15), .clk(Clock), .clr(Reset));

  // Other names for the same wires on the sheet: CLK = Clock; RD1[31:0] = Read_Data_1; RD2[31:0] = Read_Data_2;
  //   RE = Reset; RR1[4:0] = Read_Register_1; RR2[4:0] = Read_Register_2; RW = RegWrite; WD[31:0] = Write_Data;
  //   WR[4:0] = Write_Register

  // Notes on the sheet:
  //   READING
  //   WRITING
  //   OTHERS
  //   IMPUTS
  //   SENDING THE DATA
  //   OUTPUTS
  //   READING DATA
  //   SELECTING READING REGISTERS
  //   SECTION 1
  //   SECTION 2
  //   0 - 15
  //   16 - 31
endmodule

module ControlUnit (
  input  [3:0] ALUControl,
  input  RegWire,
  input  MemRead,
  input  MemWrite,
  input  [1:0] WriteSlct,
  input  ALUSrc,
  input  RegDest,
  input  [2:0] JSelct,
  input  IorD,
  input  Halt
);


  // Other names for the same wires on the sheet: AC[3:0] = ALUControl; ASrc = ALUSrc; is_halt = Halt;
  //   JSlct[2:0] = JSelct; MR = MemRead; MW = MemWrite; RDest = RegDest; RW = RegWire; WSlct[1:0] = WriteSlct

  // Notes on the sheet:
  //   INPUT
endmodule

module InstructionDecoder (
  input  [31:0] Instruction,
  output [3:0] ALUControl,
  output RegWire,
  output MemRead,
  output MemWrite,
  output [1:0] WriteSlct,
  output ALUSrc,
  output RegDest,
  output [2:0] JSelect,
  output IorD,
  output Halt
);

  wire comparator_6_eq, comparator_7_eq, comparator_8_eq, halt_func, is_addi, is_andi, is_beq, is_bgtz,
       is_blez, is_bltz, is_bne, is_j, is_jr, is_mfhi, is_mflo, is_ori, is_RPure, is_slti, is_sltiu,
       is_special, is_xori, not_1_out, not_2_out, not_3_out;
  wire [2:0] AOP;
  wire [3:0] aludecoder_1_alucontrol;

  Comparator #(.width(6)) comparator_1 (.a(Instruction[31:26]), .b(6'b000100), .eq(is_beq));  // open: gt, lt
  // Probe on 6'b000100
  Comparator #(.width(6)) comparator_2 (.a(Instruction[31:26]), .b(6'b000101), .eq(is_bne));  // open: gt, lt
  // Probe on 6'b000101
  Comparator #(.width(6)) comparator_3 (.a(Instruction[31:26]), .b(6'b000110), .eq(is_blez));  // open: gt, lt
  // Probe on 6'b000110
  Comparator #(.width(6)) comparator_4 (.a(Instruction[31:26]), .b(6'b000111), .eq(is_bgtz));  // open: gt, lt
  // Probe on 6'b000111
  Comparator #(.width(6)) comparator_5 (.a(Instruction[31:26]), .b(6'b000001), .eq(is_bltz));  // open: gt, lt
  // Probe on 6'b000001
  // Probe on {6{1'b0}}
  // Probe on 6'b100011
  // Probe on 6'b101011
  // Probe on 6'b001000
  // Probe on 6'b001100
  // Probe on 6'b001101
  // Probe on 6'b001110
  // Probe on 6'b001010
  // Probe on 6'b001011
  // Probe on 6'b000010
  Comparator #(.width(6)) comparator_6 (.a(Instruction[5:0]), .b(6'b001000), .eq(comparator_6_eq));  // open: gt, lt
  // Probe on 6'b001000
  Comparator #(.width(6)) comparator_7 (.a(Instruction[5:0]), .b(6'b010000), .eq(comparator_7_eq));  // open: gt, lt
  // Probe on 6'b010000
  Comparator #(.width(6)) comparator_8 (.a(Instruction[5:0]), .b(6'b010010), .eq(comparator_8_eq));  // open: gt, lt
  // Probe on 6'b010010
  Comparator #(.width(6)) comparator_9 (.a(Instruction[31:26]), .b({6{1'b0}}), .eq(RegDest));  // open: gt, lt
  Comparator #(.width(6)) comparator_10 (.a(Instruction[31:26]), .b(6'b100011), .eq(MemRead));  // open: gt, lt
  Comparator #(.width(6)) comparator_11 (.a(Instruction[31:26]), .b(6'b101011), .eq(MemWrite));  // open: gt, lt
  Comparator #(.width(6)) comparator_12 (.a(Instruction[31:26]), .b(6'b001000), .eq(is_addi));  // open: gt, lt
  Comparator #(.width(6)) comparator_13 (.a(Instruction[31:26]), .b(6'b001100), .eq(is_andi));  // open: gt, lt
  Comparator #(.width(6)) comparator_14 (.a(Instruction[31:26]), .b(6'b001101), .eq(is_ori));  // open: gt, lt
  Comparator #(.width(6)) comparator_15 (.a(Instruction[31:26]), .b(6'b001110), .eq(is_xori));  // open: gt, lt
  Comparator #(.width(6)) comparator_16 (.a(Instruction[31:26]), .b(6'b001010), .eq(is_slti));  // open: gt, lt
  Comparator #(.width(6)) comparator_17 (.a(Instruction[31:26]), .b(6'b001011), .eq(is_sltiu));  // open: gt, lt
  Comparator #(.width(6)) comparator_18 (.a(Instruction[31:26]), .b(6'b000010), .eq(is_j));  // open: gt, lt
  and and_1 (is_jr, RegDest, comparator_6_eq);
  and and_2 (is_mfhi, RegDest, comparator_7_eq);
  and and_3 (is_mflo, RegDest, comparator_8_eq);
  not not_1 (not_1_out, is_jr);
  and and_4 (is_RPure, RegDest, not_1_out, not_2_out, not_3_out);
  not not_2 (not_2_out, is_mfhi);
  not not_3 (not_3_out, is_mflo);
  or or_1 (IorD, MemWrite, MemRead);
  ALUDecoder aludecoder_1 (.FunCode(Instruction[5:0]), .ALUControl(aludecoder_1_alucontrol));
  or or_2 (AOP[0], RegDest, is_beq, is_slti, is_ori);
  or or_3 (AOP[1], RegDest, is_sltiu, is_andi, is_ori);
  or or_4 (AOP[2], RegDest, is_xori, is_sltiu, is_slti);
  // Probe on {6{1'b1}}
  Comparator #(.width(6)) comparator_19 (.a(Instruction[5:0]), .b({6{1'b1}}), .eq(halt_func));  // open: gt, lt
  // Probe on {6{1'b1}}
  or or_5 (RegWire, is_slti, is_RPure, MemRead, is_addi, is_andi, is_xori, is_ori, is_sltiu);
  // Probe on AOP
  Comparator #(.width(6)) comparator_20 (.a(Instruction[31:26]), .b({6{1'b1}}), .eq(is_special));  // open: gt, lt
  Multiplexer #(.select(3), .width(4), .enable("false")) multiplexer_1 (
    .in0(4'b0000), .in1(4'b0001), .in2(4'b0010), .in3(4'b0011), .in4(4'b0101), .in5(4'b0110), .in6(4'b0111),
    .in7(aludecoder_1_alucontrol), .out(ALUControl), .sel(AOP));
  and and_5 (Halt, is_special, halt_func);
  or or_6 (ALUSrc, is_slti, MemRead, MemWrite, is_addi, is_andi, is_ori, is_xori, is_sltiu);
  or or_7 (JSelect[0], is_blez, is_beq, is_bltz, is_jr);
  or or_8 (JSelect[1], is_bne, is_blez, is_j, is_jr);
  or or_9 (JSelect[2], is_bgtz, is_bltz, is_j, is_jr);
  or or_10 (WriteSlct[0], MemRead, is_mflo);
  or or_11 (WriteSlct[1], is_mfhi, is_mflo);
  // Probe on JSelect
  // Probe on WriteSlct

  // Other names for the same wires on the sheet: AC[3:0] = ALUControl; ASrc = ALUSrc; FunCode[5:0] = Instruction[5:0];
  //   INST[31:0] = Instruction; OpCode[5:0] = Instruction[31:26]; is_halt = Halt; is_lw = MemRead; MR = MemRead;
  //   is_R = RegDest; RDest = RegDest; is_sw = MemWrite; MW = MemWrite; JSlct[2:0] = JSelect; RW = RegWire;
  //   WSlct[1:0] = WriteSlct

  // Notes on the sheet:
  //   IMPUTS
  //   OUTPUTS
  //   000100
  //   000101
  //   000110
  //   000111
  //   000001
  //   is beq
  //   is bne
  //   is blez
  //   is bgtz
  //   is bltz
  //   001000
  //   010000
  //   010000
  //   01 0010
  //   OpCode
  //   000000
  //   is R type
  //   100011
  //   is lw
  //   101011
  //   is sw
  //   001000
  //   is addi
  //   001100
  //   is andi
  //   001101
  //   is ori
  //   001110
  //   is xori
  //   001010
  //   is slti
  //   001011
  //   is sltiu
  //   000010
  //   is j
  //   ALUDecoder
  //   RegWire
  //   MemoryRead
  //   Register Destination
  //   IoD
  //   111111
  //   is special
  //   ALUSrc
  //   MemoryWrite
  //   JumpSelect
  //   MemoryToReg
endmodule

module ALUDecoder (
  input  [5:0] FunCode,
  output [3:0] ALUControl
);

  wire add, \and , div, divu, mult, mulu, \not , \or , slt, sltu, sub, \xor ;

  Comparator #(.width(6)) comparator_1 (.a(FunCode), .b(6'b100000), .eq(add));  // open: gt, lt
  Comparator #(.width(6)) comparator_2 (.a(FunCode), .b(6'b100010), .eq(sub));  // open: gt, lt
  Comparator #(.width(6)) comparator_3 (.a(FunCode), .b(6'b100100), .eq(\and ));  // open: gt, lt
  Comparator #(.width(6)) comparator_4 (.a(FunCode), .b(6'b100101), .eq(\or ));  // open: gt, lt
  Comparator #(.width(6)) comparator_5 (.a(FunCode), .b(6'b100111), .eq(\not ));  // open: gt, lt
  Comparator #(.width(6)) comparator_6 (.a(FunCode), .b(6'b101000), .eq(\xor ));  // open: gt, lt
  Comparator #(.width(6)) comparator_7 (.a(FunCode), .b(6'b101010), .eq(slt));  // open: gt, lt
  Comparator #(.width(6)) comparator_8 (.a(FunCode), .b(6'b101011), .eq(sltu));  // open: gt, lt
  Comparator #(.width(6)) comparator_9 (.a(FunCode), .b(6'b011001), .eq(mulu));  // open: gt, lt
  Comparator #(.width(6)) comparator_10 (.a(FunCode), .b(6'b011000), .eq(mult));  // open: gt, lt
  Comparator #(.width(6)) comparator_11 (.a(FunCode), .b(6'b011011), .eq(divu));  // open: gt, lt
  Comparator #(.width(6)) comparator_12 (.a(FunCode), .b(6'b011010), .eq(div));  // open: gt, lt
  or or_1 (ALUControl[0], sub, \or , \xor , sltu, mult, div);
  or or_2 (ALUControl[1], \and , \or , slt, sltu, divu, div);
  or or_3 (ALUControl[2], \not , \xor , slt, sltu);
  or or_4 (ALUControl[3], mulu, mult, divu, div);

  // Other names for the same wires on the sheet: AC[3:0] = ALUControl; bit_0 = ALUControl[0]; bit_1 = ALUControl[1];
  //   bit_2 = ALUControl[2]; bit_3 = ALUControl[3]; FC[5:0] = FunCode

  // Notes on the sheet:
  //   IMPUTS
  //   100000
  //   100010
  //   100100
  //   101010
  //   101011
  //   011001
  //   011000
  //   011011
  //   011010
  //   is Add
  //   is Sub
  //   is and
  //   100101
  //   is or
  //   100111
  //   is not
  //   101000
  //   is xor
  //   is slt
  //   is sltu
  //   1000
  //   is mulu
  //   1001
  //   is mult
  //   1010
  //   is divu
  //   1011
  //   is div
  //   0000
  //   0001
  //   0010
  //   0011
  //   0100
  //   0101
  //   0110
  //   0111
  //   OUTPUTS
endmodule

module Program_Counter (
  input  [31:0] in_1,
  input  in_2,
  input  in_3,
  input  in_4,
  output [31:0] Actual_Lo
);

  wire undriven;

  Register #(.width(32)) register_1 (.D(in_1), .en(in_3), .Q(Actual_Lo), .clk(undriven), .clr(in_2));

  // Other names for the same wires on the sheet: clk = in_4; enable = in_3; PC[31:0] = Actual_Lo;
  //   PC_prime[31:0] = in_1; reset = in_2

  // Notes on the sheet:
  //   Input
  //   Processing Data
  //   Processing Data
  //   Output
endmodule

module Branch_Control (
  input  [2:0] in_1,
  input  in_2,
  input  in_3,
  input  [31:0] in_4,
  input  [25:0] in_5,
  input  [31:0] in_6,
  input  [31:0] in_7,
  output [31:0] PC_prime
);

  wire and_1_out, and_2_out, and_3_out, and_4_out, and_5_out, and_6_out, and_7_out, beq, bgtz, blez, bltz,
       bne, cond, j, jr, nop, or_1_out;
  wire [1:0] jump_select;
  wire [31:0] multiplier_1_out, PC_4, PC_4_offset_4;

  or or_1 (or_1_out, in_3, in_2);
  and and_1 (and_1_out, ~in_3, ~in_2);  // AND_Gate
  and and_2 (and_2_out, ~in_3, in_2);  // AND_Gate
  and and_3 (and_3_out, beq, in_3);
  and and_4 (and_4_out, bne, ~in_3);  // AND_Gate
  and and_5 (and_5_out, blez, or_1_out);
  and and_6 (and_6_out, bgtz, and_1_out);
  and and_7 (and_7_out, bltz, and_2_out);
  or or_2 (cond, and_3_out, and_4_out, and_5_out, and_6_out, and_7_out);
  Adder #(.width(32)) adder_1 (.a(in_4), .b(32'h4), .out(PC_4));  // open: cin, cout
  Multiplexer #(.select(2), .width(32), .enable("false")) multiplexer_1 (
    .in0(PC_4), .in1(PC_4_offset_4), .in2({in_4[31:28], in_5, 2'b00}), .in3(in_6), .out(PC_prime),
    .sel(jump_select));
  Multiplier #(.width(32)) multiplier_1 (.a(32'h4), .b(in_7), .out(multiplier_1_out));  // open: cin, cout
  Adder #(.width(32)) adder_2 (.a(PC_4), .b(multiplier_1_out), .out(PC_4_offset_4));  // open: cin, cout
  Decoder #(.select(3), .enable("false")) decoder_1 (
    .out0(nop), .out1(beq), .out2(bne), .out3(blez), .out4(bgtz), .out5(bltz), .out6(j), .out7(jr), .sel(in_1));
  Priority_Encoder #(.select(2)) priority_encoder_1 (
    .in0(1'b1), .in1(cond), .in2(j), .in3(jr), .out(jump_select), .en_in(1'b1));  // open: gs, en_out

  // Other names for the same wires on the sheet: destino[31:2] = {in_4[31:28], in_5}; jump_size[25:0] = in_5;
  //   PC[31:0] = in_4; offset[31:0] = in_7; RS[31:0] = in_6; select_jump_type[2:0] = in_1; sing_flag = in_2;
  //   zero_flag = in_3

  // Notes on the sheet:
  //   Inputs
  //   Checking Conditon
  //   Output
  //   Processing Data
  //   Select the Jump Type
  //   Select the Jump
endmodule

module Chronometer (
  input  in_1,
  input  in_2,
  input  in_3,
  input  [3:0] in_4,
  output Counting,
  output Cicle_Finished
);

  wire comparator_1_eq, d_ff_1_q, or_1_out;
  wire [4:0] counter_1_q;

  Clock clock_1 ();  // open: out
  Counter #(.width(5), .max('h1f)) counter_1 (
    .load(1'b0), .count(in_2), .Q(counter_1_q), .clk(in_1), .clr(or_1_out));  // open: D, carry
  Comparator #(.width(5)) comparator_1 (.a(counter_1_q), .b({5{1'b0}}), .eq(comparator_1_eq));  // open: gt, lt
  Comparator #(.width(5)) comparator_2 (.a({1'b0, in_4}), .b(counter_1_q), .eq(Cicle_Finished));  // open: gt, lt
  or or_1 (or_1_out, d_ff_1_q, in_3);
  or or_2 (Counting, ~comparator_1_eq, in_2);  // OR_Gate
  D_Flip_Flop #(.trigger("falling")) d_ff_1 (
    .clk(in_1), .D(Cicle_Finished), .Q(d_ff_1_q), .reset(or_1_out));  // open: Qn, preset, en

  // Other names for the same wires on the sheet: Frecuency[3:0] = in_4; Clock = in_1; END = Cicle_Finished;
  //   Reset_Signal = in_3; Start_Signal = in_2

  // Notes on the sheet:
  //   INPUTS
  //   OUTPUTS
endmodule

module Helpers (
  input  in_1,
  input  [25:0] in_2
);

  // OR_Gate or_1 is placed but not wired
  // AND_Gate and_1 is placed but not wired
  Multiplexer #(.select(2), .width(32), .enable("false")) multiplexer_1 ();  // open: in0, in1, in2, in3, out, sel
  Adder #(.width(32)) adder_1 ();  // open: a, b, out, cin, cout

  // Notes on the sheet:
  //   Qué mirás bobo!?
  //   Andá pashá!
endmodule

module Instruction_Decoder (
  input  [31:0] in_1,
  output [25:0] out_2,
  output [5:0] out_3,
  output [15:0] out_4,
  output [4:0] out_5,
  output [4:0] out_6,
  output [4:0] out_7,
  output [5:0] out_8
);


  assign out_2 = in_1[25:0];
  assign out_3 = in_1[31:26];
  assign out_4 = in_1[15:0];
  assign out_5 = in_1[20:16];
  assign out_6 = in_1[25:21];
  assign out_7 = in_1[15:11];
  assign out_8 = in_1[5:0];

  // Other names for the same wires on the sheet: const[15:0] = in_1[15:0]; destino_salto[25:0] = in_1[25:0];
  //   func_code[5:0] = in_1[5:0]; instruction[31:0] = in_1; Rd[4:0] = in_1[15:11]; Rt[4:0] = in_1[20:16];
  //   Rs[4:0] = in_1[25:21]; op_code[5:0] = in_1[31:26]
endmodule

module RAM_manager (
  input  [31:0] in_1,
  input  in_2,
  input  in_3,
  input  in_4,
  input  [31:0] in_5,
  input  [31:0] in_6,
  input  [31:0] in_7,
  input  [31:0] in_8,
  input  [31:0] RAM_In,
  output [15:0] Adress_Out,
  output [3:0] mask,
  output [31:0] Output,
  output [31:0] out_13,
  output [31:0] out_14,
  output [31:0] out_15,
  output [31:0] out_16
);

  wire [1:0] Bank;
  wire [15:2] divider_1_rem;
  wire [31:0] shifter_1_out;

  Shifter #(.width(32), .shift("lr")) shifter_1 (.in(in_1), .\dist (5'b00010), .out(shifter_1_out));
  Divider #(.width(16)) divider_1 (
    .a(shifter_1_out[15:0]), .b(16'h4), .out(Adress_Out), .rem({divider_1_rem, Bank}));  // open: upper
  Multiplexer #(.select(2), .width(32), .enable("false")) multiplexer_1 (
    .in0(in_5), .in1(in_7), .in2(in_6), .in3(in_8),
    .out({Output[7:0], Output[15:8], Output[23:16], Output[31:24]}), .sel(Bank));
  Register #(.width(32)) register_1 (
    .D(RAM_In), .en(in_4), .Q({out_13[7:0], out_13[15:8], out_13[23:16], out_13[31:24]}), .clk(in_2),
    .clr(in_3));
  Decoder #(.select(2), .enable("false")) decoder_1 (
    .out0(mask[0]), .out1(mask[1]), .out2(mask[2]), .out3(mask[3]), .sel(Bank));

  assign out_14 = out_13;
  assign out_15 = out_13;
  assign out_16 = out_13;

  // Other names for the same wires on the sheet: clk = in_2; RAM_00[31:0] = in_5; RAM_01[31:0] = in_7;
  //   RAM_02[31:0] = in_6; RAM_03[31:0] = in_8; rst = in_3; save_data = in_4

  // Notes on the sheet:
  //   Adress in
endmodule
